# Fritzing sketch Untitled Sketch 2.fzzproject circuit (saved by Fritzing 0.9.3b)
circuit board: 11.4242cm x 9.75925cm
breadboards: 2

parts:
  Part1 = Arduino Uno (Rev3)
  CONVERTER1 = Mini-360 DC-DC Buck converter [package=THT]
  GSM_SIM800L1 = SIM800L BO
  R8 = Resistor [tolerance=±5% resistance=10k package="2512 [SMD]"]
  R9 = Resistor [tolerance=±5% resistance=10k package="2512 [SMD]"]
  GPS_MODULE1 = SUP500F [package=sup500f]
  R11 = Resistor [tolerance=±5% resistance=4.7k package="1206 [SMD]"]
  R12 = Resistor [tolerance=±5% resistance=10k package="1206 [SMD]"]
  S1 = Round Pushbutton
  R13 = Resistor [tolerance=±5% resistance=10k package="2512 [SMD]"]

nets (from the pcb view):
  N1: Part1.D8, GPS_MODULE1.VCC
  N2: Part1.D10_PWM/SS, R12.Pin_1
  N3: Part1.GND, GPS_MODULE1.RX-I, R11.Pin_0, S1.leg1, R13.Pin_0
  N4: Part1.D2, S1.leg0, R13.Pin_1
  N5: Part1.D4, GSM_SIM800L1.pin_5
  N6: Part1.D6_PWM, R9.Pin_0
  N7: Part1.5V, GPS_MODULE1.TX-O
  N8: CONVERTER1.IN-, R8.Pin_1
  N9: CONVERTER1.OUT+, GSM_SIM800L1.PIN2
  N10: CONVERTER1.OUT-, GSM_SIM800L1.pin_6
  N11: GSM_SIM800L1.pin_4, R8.Pin_0, R9.Pin_1
  N12: GPS_MODULE1.GND, R11.Pin_1, R12.Pin_0

notes:
  GND: Black
  VCC: Red
  RX: Yellow
  TX: Green

custom parts:
  Mini-360 DC-DC Buck converter: Mini-360 DC-DC Buck converter. Tiny buck step down voltage converter, input voltage 4.75 to 23V output 1 to 17V adjustable. Available from ebay and the like.
